# Fritzing sketch hbridge_motor (saved by Fritzing 0.9.10b)

parts:
  S1 = H-Bridge with L298N
  Mod1 = Raspberry Pi Pico
  M1 = DC Motor [voltage_(max)=6V voltage_(min)=3V]
  VCC1 = Battery

nets:
  N1: S1.12V, VCC1.+
  N2: S1.GND, S1.IN1, Mod1.pin_3, Mod1.pin_8, Mod1.pin_18, Mod1.pin_42, VCC1.-
  N3: S1.ENA, Mod1.pin_2
  N4: S1.IN2, Mod1.pin_4
  N5: S1.M1-01, M1.pin_2
  N6: S1.M1-02, M1.pin_1

notes:
  Power Source +12V

custom parts:
  H-Bridge with L298N: h-bridge
  Raspberry Pi Pico: Raspberry Pi Pico. Based around the RP2040 microcontroller the Pico is a low cost microcontroller device bringing Raspberry Pi quality, cost, and easy of use to the microcontroller space. Jan 2021, Split part in to two versions: SMD (this one) and tht. This one is single sided and uses the castellation pads to solder the module to the board (no holes, other than for the USB connector!). The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
